# Fritzing sketch Fob Reader (saved by Fritzing 0.9.3b)
circuit board: 7.08031cm x 11.5719cm
breadboards: 2

parts:
  Arduino_Micro = Arduino Micro (Rev3)
  J2 = screw terminal, 4 pins
  J1 = female pin header, 8 pins [form="♀ (female)"]
  LED1 = LED - 5mm [color="Red (633nm)" package="5 mm [THT]"]
  LED2 = LED - 5mm [color="Green (570nm)" package="5 mm [THT]"]
  J3 = Piezo Speaker
  R1 = Resistor [tolerance=±5% resistance=4.7k package=THT]
  R2 = Resistor [tolerance=±5% resistance=4.7k package=THT]
  J4 = male pin header, 3 pins [form="♂ (male)"]
  J5 = male pin header, 3 pins [form="♂ (male)"]
  J6 = male pin header, 3 pins [form="♂ (male)"]

nets:
  N1: Arduino_Micro.MOSI, J1.pin4
  N2: Arduino_Micro.GND, J2.pin4, J1.pin6, LED1.cathode, LED2.cathode, J3.pin1, J4.pin1, J5.pin1, J6.pin1
  N3: Arduino_Micro.D2/SDA, J2.pin2, R1.Pin_0
  N4: Arduino_Micro.D3/SCL, J2.pin1, R2.Pin_0
  N5: Arduino_Micro.D5_PWM, J3.pin2
  N6: Arduino_Micro.D6_PWM/A7, LED2.anode
  N7: Arduino_Micro.D7, LED1.anode
  N8: Arduino_Micro.D8_PWM/A8, J1.pin7
  N9: Arduino_Micro.D9_PWM/A9, J4.pin2
  N10: Arduino_Micro.D10_PWM/A10, J5.pin2
  N11: Arduino_Micro.D11_PWM, J6.pin2
  N12: Arduino_Micro.D12_PWM/A11, J1.pin2
  N13: Arduino_Micro.SCK, J1.pin3
  N14: Arduino_Micro.MISO, J1.pin5
  N15: Arduino_Micro.5V, J2.pin3, R1.Pin_1, R2.Pin_1, J4.pin3, J5.pin3, J6.pin3
  N16: Arduino_Micro.3V3, J1.pin8

notes:
  CyGate4 - Fob Reader, Proximity Fob Reader for CyGate4, 1.0
  Gnd
  +5V
  SCL
  SDA
  To MiFare RC522
  PWR
  Scan
  +3.3V
  RST
  MISO
  MOSI
  SCK
  CS
  N/C
  FAB 001001 ASSY 001001
  To MFRC522
  MFRC522 to CyGate4 Prox Reader Rev 1.0
  Copyright (c) 2021 Cyrus Brunner
  www.cyrusbuilt.net
  +
  -
  A0
  A1
  A2
  ADDR
  Address Select
  Piezo
